# Fritzing sketch SensorPlatform (saved by Fritzing 0.9.1b)
breadboards: 1

parts:
  Part1 = Photon
  PART1 = SparkFun Soil Moisture Sensor [part_number=SEN-13322]

nets:
  N1: Part1.A0, PART1.SIG
  GND: Part1.GND, PART1.GND
  3V3: Part1.3V3, PART1.VCC

custom parts:
  SparkFun Soil Moisture Sensor: The SparkFun Soil Moisture Sensor is a simple breakout for measuring the moisture in soil and similar materials.
